// Logisim project lab2.circ as structural Verilog: 1 circuit, main circuit main
module main (
);

  wire and_1_out, and_2_out, and_3_out, and_4_out, and_5_out, and_6_out, and_7_out, and_8_out, and_9_out,
       and_10_out, and_11_out, clock_1_out, clock_2_out, clock_3_out, clock_4_out, not_1_out, not_2_out,
       not_3_out, not_4_out, not_5_out, not_6_out, not_7_out, not_8_out, not_9_out, not_10_out, or_1_out,
       or_2_out, or_3_out, or_4_out, or_5_out, or_6_out, x3T2_out, x4T4_out, x7T1_out, x8T3_out, xor_1_out,
       xor_2_out, xor_3_out, xor_4_out, xor_5_out, xor_6_out, xor_7_out;

  not not_1 (not_1_out, 1'b1);
  not not_2 (not_2_out, 1'b1);
  not not_3 (not_3_out, 1'b1);
  not not_4 (not_4_out, 1'b1);
  not not_5 (not_5_out, 1'b1);
  not not_6 (not_6_out, 1'b0);
  not not_7 (not_7_out, 1'b0);
  not not_8 (not_8_out, 1'b1);
  Clock clock_1 (.out(clock_1_out));
  Clock #(.lowDuration(3)) clock_2 (.out(clock_2_out));
  Clock #(.lowDuration(5)) clock_3 (.out(clock_3_out));
  or or_1 (or_1_out, 1'b1, 1'b1);
  or or_2 (or_2_out, 1'b1, 1'b0);
  Clock #(.lowDuration(7)) clock_4 (.out(clock_4_out));
  and x3T2 (x3T2_out, clock_2_out, 1'b1);
  and x4T4 (x4T4_out, clock_4_out, 1'b1);
  and x7T1 (x7T1_out, clock_1_out, 1'b0);
  and x8T3 (x8T3_out, clock_3_out, 1'b1);
  or or_3 (or_3_out, x3T2_out, x4T4_out);
  or or_4 (or_4_out, x7T1_out, x8T3_out);
  xor xor_1 (xor_1_out, 1'b1, 1'b1);
  xor xor_2 (xor_2_out, xor_1_out, 1'b1);
  or or_5 (or_5_out, or_3_out, or_1_out);
  or or_6 (or_6_out, or_4_out, or_2_out);
  xor xor_3 (xor_3_out, xor_2_out, 1'b1);
  not not_9 (not_9_out, or_6_out);
  xor xor_4 (xor_4_out, xor_3_out, 1'b1);
  and and_1 (and_1_out, 1'b1, 1'b1);
  xor xor_5 (xor_5_out, xor_4_out, 1'b0);
  xor xor_6 (xor_6_out, xor_5_out, 1'b0);
  xor xor_7 (xor_7_out, xor_6_out, 1'b1);
  and and_2 (and_2_out, clock_2_out, not_1_out);
  LED led_1 (.in(and_2_out));
  and and_3 (and_3_out, clock_2_out, not_2_out);
  LED led_2 (.in(and_3_out));
  and and_4 (and_4_out, clock_2_out, not_3_out);
  LED led_3 (.in(and_4_out));
  and and_5 (and_5_out, clock_2_out, not_4_out);
  LED led_4 (.in(and_5_out));
  and and_6 (and_6_out, clock_2_out, not_5_out);
  LED led_5 (.in(and_6_out));
  and and_7 (and_7_out, clock_2_out, not_6_out);
  LED led_6 (.in(and_7_out));
  and and_8 (and_8_out, clock_2_out, not_7_out);
  LED led_7 (.in(and_8_out));
  and and_9 (and_9_out, clock_2_out, not_8_out);
  LED led_8 (.in(and_9_out));
  and and_10 (and_10_out, or_5_out, not_9_out);
  LED led_9 (.in(and_10_out));
  and and_11 (and_11_out, and_1_out, 1'b1);
  LED led_10 (.in(and_11_out));
  not not_10 (not_10_out, xor_7_out);
  LED led_11 (.in(not_10_out));

  // Notes on the sheet:
  //   x1
  //   x2
  //   x3
  //   x4
  //   x5
  //   x6
  //   x7
  //   x8
  //   !x1
  //   !x2
  //   !x3
  //   !x4
  //   !x5
  //   !x6
  //   !x7
  //   !x8
  //   T1
  //   T2
  //   x1|x2
  //   x5|x6
  //   T3
  //   T4
  //   (x3&T2)|(x4&T4)
  //   (x7&T1)|(x8&T3))
  //   (x1|x2|(x3&T2)|(x4&T4))
  //   !(x5|x6|(x7&T1)|(x8&T3))
  //   x1&x2&x5
  //   y1
  //   y2
  //   y3
  //   y4
  //   y5
  //   y6
  //   y7
  //   y8
  //   y9
  //   y10
  //   y11
endmodule
